# Fritzing sketch Gardenr (saved by Fritzing 0.9.3b)
circuit board: 5.84359cm x 4.83459cm
breadboards: 1

parts:
  MCP3008 = MCP3008 [package=dil16]
  SHT-21 = female pin header, 4 pins [form="♀ (female)"]
  J2 = double row female pin header, 40 pins [form="♀ (female)"]
  SOIL = female pin header, 3 pins [form="♀ (female)"]
  LCD = female pin header, 4 pins [form="♀ (female)"]

nets:
  N1: MCP3008.CH0, SOIL.pin1
  N2: MCP3008.DGND, SHT-21.pin4, J2.pin23, SOIL.pin3, LCD.pin4
  N3: MCP3008.CS/SHDN, J2.pin32
  N4: MCP3008.Din, J2.pin11
  N5: MCP3008.Dout, J2.pin10
  N6: MCP3008.CLK, J2.pin9
  N7: MCP3008.AGND, J2.pin16
  N8: MCP3008.VREF, MCP3008.VDD, J2.pin20
  N9: SHT-21.pin1, J2.pin18, LCD.pin1
  N10: SHT-21.pin2, J2.pin19, LCD.pin2
  N11: SHT-21.pin3, J2.pin12
  N12: J2.pin21, SOIL.pin2, LCD.pin3
